# Fritzing sketch wemos_project (saved by Fritzing 0.9.3b)
breadboards: 1

parts:
  WeMos_D1_R1 = WeMos D1 R2
  Componente1 = MicroSD Card Module
  R1 = Resistor [tolerance=±5% resistance=10k package="2010 [SMD]"]
  R2 = Resistor [tolerance=±5% resistance=10k package="2010 [SMD]"]
  R3 = Resistor [tolerance=±5% resistance=10k package="2010 [SMD]"]
  R4 = Resistor [tolerance=±5% resistance=10k package="2010 [SMD]"]
  DS1 = DS18B20 1-Wire Temperature Sensor [part_number=DS18B20]
  R5 = Resistor [tolerance=±5% resistance=10k package="2010 [SMD]"]
  M1 = sim800L v2 evb

nets:
  N1: WeMos_D1_R1.D2, DS1.DQ, R5.Pin_0
  GND: WeMos_D1_R1.D3, WeMos_D1_R1.D4, Componente1.GND, R1.Pin_1, R2.Pin_1, R3.Pin_1, R4.Pin_1, DS1.GND, M1.pin_1, M1.pin_2, M1.pin_3, M1.pin_4, M1.pin_6
  N2: WeMos_D1_R1.(D5), Componente1.SCK, R3.Pin_0
  N3: WeMos_D1_R1.(D6), Componente1.MISO, R1.Pin_0
  N4: WeMos_D1_R1.(D7), Componente1.MOSI, R2.Pin_0
  N5: WeMos_D1_R1.D8, Componente1.CS
  VCC: Componente1.VCC, DS1.VDD, R5.Pin_1

custom parts:
  WeMos D1 R2: The D1 R2 is a mini wifi board based on the ESP-8266EX.
  sim800L v2 evb: sim800L v2 evb GSM module.
